// Logisim project lab3.circ as structural Verilog: 8 circuits, main circuit toy_cpu
module toy_cpu (
  input  in_1,
  input  in_2,
  input  reset,
  input  [7:0] in_4,
  input  [7:0] in_5,
  input  in_6,
  output out_7,
  output [7:0] out_8
);

  wire adder_2_cout, clock_1_out, control_unit_1_load_memory, control_unit_1_reg_write, control_unit_1_store,
       or_1_out, or_2_out_3;
  wire [7:0] adder_1_out, adder_2_out, bit_extender_1_out, bit_extender_2_out, register_1_q, xor_1_out;
  wire [15:0] alu_1_out_4, multiplexer_1_out, ram_1_data, reg_file_1_read_1_output, reg_file_1_read_2_output,
       reg_file_1_write_val, rom_1_data;

  Adder adder_1 (.a(register_1_q), .b(8'h1), .out(adder_1_out));  // open: cin, cout
  // Probe on adder_1_out
  Register register_1 (.D(adder_1_out), .Q(register_1_q), .clk(clock_1_out), .clr(reset));  // open: en
  Clock clock_1 (.out(clock_1_out));
  // Probe on rom_1_data[15:12]
  ROM #(.dataWidth(16)) rom_1 (.addr(register_1_q), .data(rom_1_data));  // open: sel
  // Probe on reg_file_1_write_val
  reg_file reg_file_1 (
    .write_input(multiplexer_1_out), .write(control_unit_1_reg_write), .write_address(rom_1_data[11:8]),
    .clock(clock_1_out), .read_1(rom_1_data[7:4]), .read_2(rom_1_data[3:0]),
    .read_1_output(reg_file_1_read_1_output), .read_2_output(reg_file_1_read_2_output),
    .write_val(reg_file_1_write_val));
  Control_Unit control_unit_1 (
    .in_1(rom_1_data[15:12]), .store(control_unit_1_store), .load_memory(control_unit_1_load_memory),
    .reg_write(control_unit_1_reg_write));  // open: load_address, store_indirect, load_indirect
  // Probe on control_unit_1_store
  // Probe on control_unit_1_load_memory
  // Probe on alu_1_out_4
  ALU alu_1 (
    .input_1(reg_file_1_read_1_output), .input_2(reg_file_1_read_2_output), .ALU_op(rom_1_data[14:12]),
    .out_4(alu_1_out_4));
  or or_1 (or_1_out, control_unit_1_store, control_unit_1_load_memory);
  RAM #(.dataWidth(16), .bus("separate")) ram_1 (
    .addr(rom_1_data[7:0]), .din(reg_file_1_write_val), .data(ram_1_data), .str(control_unit_1_store),
    .sel(or_1_out), .clk(clock_1_out), .ld(control_unit_1_load_memory));  // open: clr
  // Probe on multiplexer_1_out
  Multiplexer #(.width(16)) multiplexer_1 (
    .in0(alu_1_out_4), .in1(ram_1_data), .out(multiplexer_1_out), .sel(control_unit_1_load_memory));  // open: en
  assign bit_extender_1_out = {{7{in_6}}, in_6};  // Bit_Extender bit_extender_1
  \or  or_2 (.in_1(in_1), .in_2(in_2), .out_3(or_2_out_3));
  assign bit_extender_2_out = {{7{1'b0}}, in_6};  // Bit_Extender bit_extender_2
  assign xor_1_out = in_5 ^ bit_extender_1_out;  // XOR_Gate xor_1, 8 bits wide
  Adder adder_2 (.a(xor_1_out), .b(bit_extender_2_out), .out(adder_2_out), .cout(adder_2_cout));  // open: cin
  \not  not_1 (.in_1(or_2_out_3), .out_2(out_7));
  Adder adder_3 (.a(in_4), .b(adder_2_out), .out(out_8));  // open: cin, cout

  // Notes on the sheet:
  //   contents of rom_1 (hex, n*v repeats v):
  //   8132 8233 4112 4212 4112 9132 9233 8131
endmodule

module \not  (
  input  in_1,
  output out_2
);

  Pull_Resistor pull_resistor_1 (.node(out_2));
  Transistor transistor_1 (.in(1'b1), .out(out_2), .gate(in_1));
endmodule

module \or  (
  input  in_1,
  input  in_2,
  output out_3
);

  Pull_Resistor pull_resistor_1 (.node(out_3));
  Transistor #(.\type ("n")) transistor_1 (.in(1'b1), .out(out_3), .gate(in_1));
  Transistor #(.\type ("n")) transistor_2 (.in(1'b1), .out(out_3), .gate(in_2));
  Pull_Resistor pull_resistor_2 (.node(out_3));
endmodule

module _1_bit_register (
  input  clock,
  input  data_in,
  input  write_enable,
  output out_4
);

  wire d_ff_1_q;

  D_Flip_Flop d_ff_1 (.clk(clock), .D(out_4), .Q(d_ff_1_q));  // open: Qn, preset, en, reset
  Multiplexer #(.enable("false")) multiplexer_1 (.in0(d_ff_1_q), .in1(data_in), .out(out_4), .sel(write_enable));
endmodule

module _16_bit_register (
  input  clock,
  input  write,
  input  [15:0] \input ,
  output [15:0] out_4
);

  _1_bit_register u_1_bit_register_1 (.clock(clock), .data_in(\input [0]), .write_enable(write), .out_4(out_4[0]));
  _1_bit_register u_1_bit_register_2 (.clock(clock), .data_in(\input [1]), .write_enable(write), .out_4(out_4[1]));
  _1_bit_register u_1_bit_register_3 (.clock(clock), .data_in(\input [2]), .write_enable(write), .out_4(out_4[2]));
  _1_bit_register u_1_bit_register_4 (.clock(clock), .data_in(\input [3]), .write_enable(write), .out_4(out_4[3]));
  _1_bit_register u_1_bit_register_5 (.clock(clock), .data_in(\input [4]), .write_enable(write), .out_4(out_4[4]));
  _1_bit_register u_1_bit_register_6 (.clock(clock), .data_in(\input [5]), .write_enable(write), .out_4(out_4[5]));
  _1_bit_register u_1_bit_register_7 (.clock(clock), .data_in(\input [6]), .write_enable(write), .out_4(out_4[6]));
  _1_bit_register u_1_bit_register_8 (.clock(clock), .data_in(\input [7]), .write_enable(write), .out_4(out_4[7]));
  // _1_bit_register 1_bit_register_9: pin names not known; wires that end beside it: clock, clock, \input [8], write, out_4[8]
  // _1_bit_register 1_bit_register_10: pin names not known; wires that end beside it: clock, clock, \input [9], write, out_4[9]
  // _1_bit_register 1_bit_register_11: pin names not known; wires that end beside it: clock, clock, \input [10], write, out_4[10]
  // _1_bit_register 1_bit_register_12: pin names not known; wires that end beside it: clock, \input [11], write, out_4[11]
  _1_bit_register u_1_bit_register_13 (.clock(clock), .data_in(\input [12]), .write_enable(write), .out_4(out_4[12]));
  _1_bit_register u_1_bit_register_14 (.clock(clock), .data_in(\input [13]), .write_enable(write), .out_4(out_4[13]));
  _1_bit_register u_1_bit_register_15 (.clock(clock), .data_in(\input [14]), .write_enable(write), .out_4(out_4[14]));
  _1_bit_register u_1_bit_register_16 (.clock(clock), .data_in(\input [15]), .write_enable(write), .out_4(out_4[15]));
endmodule

module reg_file (
  input  [15:0] write_input,
  input  write,
  input  [3:0] read_1,
  input  [3:0] write_address,
  input  clock,
  input  [3:0] read_2,
  output [15:0] read_1_output,
  output [15:0] read_2_output,
  output [15:0] write_val
);

  wire decoder_1_out0, decoder_1_out1, decoder_1_out2, decoder_1_out3, decoder_1_out4, decoder_1_out5,
       decoder_1_out6, decoder_1_out7, decoder_1_out8, decoder_1_out9, decoder_1_out10, decoder_1_out11,
       decoder_1_out12, decoder_1_out13, decoder_1_out14, decoder_1_out15;
  wire [15:0] t1, t2, t3, t4, t5, t6, t7, t8, t9, t10, t11, t12, t13, t14, t15, t16;

  Decoder #(.select(4), .disabled(0)) decoder_1 (
    .out0(decoder_1_out0), .out1(decoder_1_out1), .out2(decoder_1_out2), .out3(decoder_1_out3),
    .out4(decoder_1_out4), .out5(decoder_1_out5), .out6(decoder_1_out6), .out7(decoder_1_out7),
    .out8(decoder_1_out8), .out9(decoder_1_out9), .out10(decoder_1_out10), .out11(decoder_1_out11),
    .out12(decoder_1_out12), .out13(decoder_1_out13), .out14(decoder_1_out14), .out15(decoder_1_out15),
    .sel(write_address), .en(write));
  Register #(.width(16)) register_1 (.D(write_input), .en(decoder_1_out0), .Q(t1), .clk(clock));  // open: clr
  Register #(.width(16)) register_2 (.D(write_input), .en(decoder_1_out1), .Q(t2), .clk(clock));  // open: clr
  Register #(.width(16)) register_3 (.D(write_input), .en(decoder_1_out2), .Q(t3), .clk(clock));  // open: clr
  Register #(.width(16)) register_4 (.D(write_input), .en(decoder_1_out3), .Q(t4), .clk(clock));  // open: clr
  Register #(.width(16)) register_5 (.D(write_input), .en(decoder_1_out4), .Q(t5), .clk(clock));  // open: clr
  Register #(.width(16)) register_6 (.D(write_input), .en(decoder_1_out5), .Q(t6), .clk(clock));  // open: clr
  Register #(.width(16)) register_7 (.D(write_input), .en(decoder_1_out6), .Q(t7), .clk(clock));  // open: clr
  Register #(.width(16)) register_8 (.D(write_input), .en(decoder_1_out7), .Q(t8), .clk(clock));  // open: clr
  Register #(.width(16)) register_9 (.D(write_input), .en(decoder_1_out8), .Q(t9), .clk(clock));  // open: clr
  Register #(.width(16)) register_10 (.D(write_input), .en(decoder_1_out9), .Q(t10), .clk(clock));  // open: clr
  Register #(.width(16)) register_11 (.D(write_input), .en(decoder_1_out10), .Q(t11), .clk(clock));  // open: clr
  Register #(.width(16)) register_12 (.D(write_input), .en(decoder_1_out11), .Q(t12), .clk(clock));  // open: clr
  Register #(.width(16)) register_13 (.D(write_input), .en(decoder_1_out12), .Q(t13), .clk(clock));  // open: clr
  Register #(.width(16)) register_14 (.D(write_input), .en(decoder_1_out13), .Q(t14), .clk(clock));  // open: clr
  Register #(.width(16)) register_15 (.D(write_input), .en(decoder_1_out14), .Q(t15), .clk(clock));  // open: clr
  Register #(.width(16)) register_16 (.D(write_input), .en(decoder_1_out15), .Q(t16), .clk(clock));  // open: clr
  Multiplexer #(.select(4), .width(16), .enable("false")) multiplexer_1 (
    .in0(t1), .in1(t2), .in2(t3), .in3(t4), .in4(t5), .in5(t6), .in6(t7), .in7(t8), .in8(t9), .in9(t10),
    .in10(t11), .in11(t12), .in12(t13), .in13(t14), .in14(t15), .in15(t16), .out(read_1_output), .sel(read_1));
  Multiplexer #(.select(4), .width(16), .enable("false")) multiplexer_2 (
    .in0(t1), .in1(t2), .in2(t3), .in3(t4), .in4(t5), .in5(t6), .in6(t7), .in7(t8), .in8(t9), .in9(t10),
    .in10(t11), .in11(t12), .in12(t13), .in13(t14), .in14(t15), .in15(t16), .out(write_val),
    .sel(write_address));
  Multiplexer #(.select(4), .width(16), .enable("false")) multiplexer_3 (
    .in0(t1), .in1(t2), .in2(t3), .in3(t4), .in4(t5), .in5(t6), .in6(t7), .in7(t8), .in8(t9), .in9(t10),
    .in10(t11), .in11(t12), .in12(t13), .in13(t14), .in14(t15), .in15(t16), .out(read_2_output), .sel(read_2));

  // Other names for the same wires on the sheet: write_addr[3:0] = write_address; write_data[15:0] = write_input;
  //   write_enable = write
endmodule

module ALU (
  input  [15:0] input_1,
  input  [15:0] input_2,
  input  [2:0] ALU_op,
  output [15:0] out_4
);

  wire [15:0] adder_1_out, and_1_out, shifter_1_out, shifter_2_out, subtractor_1_out, xor_1_out;

  assign and_1_out = input_1 & input_2;  // AND_Gate and_1, 16 bits wide
  assign xor_1_out = input_1 ^ input_2;  // XOR_Gate xor_1, 16 bits wide
  Shifter #(.width(16)) shifter_1 (.in(input_1), .\dist (input_2[3:0]), .out(shifter_1_out));
  Shifter #(.width(16), .shift("lr")) shifter_2 (.in(input_1), .\dist (input_2[3:0]), .out(shifter_2_out));
  Adder #(.width(16)) adder_1 (.a(input_1), .b(input_2), .out(adder_1_out));  // open: cin, cout
  Subtractor #(.width(16)) subtractor_1 (.a(input_1), .b(input_2), .out(subtractor_1_out));  // open: bin, bout
  Multiplexer #(.select(3), .width(16)) multiplexer_1 (
    .in1(adder_1_out), .in2(subtractor_1_out), .in3(and_1_out), .in4(xor_1_out), .in5(shifter_1_out),
    .in6(shifter_2_out), .out(out_4), .sel(ALU_op));  // open: in0, in7, en

  // Other names for the same wires on the sheet: S[15:0] = input_1; T[15:0] = input_2
endmodule

module Control_Unit (
  input  [3:0] in_1,
  output store,
  output load_address,
  output load_memory,
  output reg_write,
  output store_indirect,
  output load_indirect
);

  wire decoder_1_out1, decoder_1_out2, decoder_1_out3, decoder_1_out4, decoder_1_out5, decoder_1_out6;

  Decoder #(.select(4)) decoder_1 (
    .out1(decoder_1_out1), .out2(decoder_1_out2), .out3(decoder_1_out3), .out4(decoder_1_out4),
    .out5(decoder_1_out5), .out6(decoder_1_out6), .out7(load_address), .out8(load_memory), .out9(store),
    .out10(load_indirect), .out11(store_indirect), .sel(in_1));  // open: out0, out12, out13, out14, out15, en
  or or_1 (reg_write, decoder_1_out1, decoder_1_out2, decoder_1_out3, decoder_1_out4, decoder_1_out5, decoder_1_out6, load_address, load_memory, load_indirect);
endmodule
